# Fritzing sketch carrinho (saved by Fritzing 0.9.3b)
circuit board: 8.46667cm x 5.64444cm

parts:
  Componente1 = Arduino Uno (Rev3) - ICSP
  L298N1 = L298N motor driver
  M1 = prefix0000
  M2 = prefix0000
  HC-SR04_Sensor_1 = HC-SR04 Ultrasonic Distance Sensor
  HC-SR04_Sensor_2 = HC-SR04 Ultrasonic Distance Sensor
  HC-SR04_Sensor_3 = HC-SR04 Ultrasonic Distance Sensor
  VCC1 = Battery block 9V

nets:
  N1: Componente1.A0, HC-SR04_Sensor_2.ECHO
  N2: Componente1.A1, HC-SR04_Sensor_2.TRIG
  N3: Componente1.A2, HC-SR04_Sensor_1.ECHO
  N4: Componente1.A3, HC-SR04_Sensor_1.TRIG
  N5: Componente1.A4/SDA, HC-SR04_Sensor_3.ECHO
  N6: Componente1.A5/SCL, HC-SR04_Sensor_3.TRIG
  GND: Componente1.GND, L298N1.connector6, HC-SR04_Sensor_1.GND, HC-SR04_Sensor_2.GND, HC-SR04_Sensor_3.GND
  N7: Componente1.D10_PWM/SS, L298N1.connector11
  N8: Componente1.D11_PWM/MOSI, L298N1.connector12
  N9: Componente1.D2, L298N1.connector13
  N10: Componente1.D3_PWM, L298N1.connector14
  N11: Componente1.D4, L298N1.connector15
  N12: Componente1.D5_PWM, L298N1.connector16
  VCC: Componente1.5V, HC-SR04_Sensor_1.VCC, HC-SR04_Sensor_2.VCC, HC-SR04_Sensor_3.VCC
  N13: Componente1.VIN, VCC1.+
  N14: L298N1.connector0, M1.connector1
  N15: L298N1.connector1, M1.connector2
  N16: L298N1.connector2, M2.connector1
  N17: L298N1.connector4, M2.connector2
